# Fritzing sketch Fritzing_sensorr1111 (saved by Fritzing 0.9.3b)
breadboards: 1

parts:
  FINGER_PRINT_1 = Fingerprint Sensor
  U1 = ESP32-38PinWide [part_number=ESP32-38PinWide]
  LED = LED - 5mm [color="Red (633nm)" package="5 mm [THT]"]
  LED_2 = LED - 5mm [color="Green (555nm)" package="5 mm [THT]"]
  LCM1602_IIC2 = LCM1602 IIC [part_number="LCM1602 IIC" chip_label="LCM1602 IIC" package="DIP (Dual Inline) [THT]"]
  LCD_16x2_12C = LCD screen
  R1 = Resistor [tolerance=±5% resistance=220 package="1206 [SMD]"]
  R2 = Resistor [tolerance=±5% resistance=220 package="1206 [SMD]"]
  Relay_1_Channel1 = 1 chan 5v relay module
  Selenoid_Door_Lock = Solenoid
  POWER_SUPPLY_12V_5A = PowerBRICK 12V
  BUZZER = Buzzer
  S1 = Square Pushbutton

nets:
  VCC: FINGER_PRINT_1.VCC, U1.VIN, LCM1602_IIC2.VCC, Relay_1_Channel1.pin_1
  N1: FINGER_PRINT_1.TX, U1.GPIO3
  N2: FINGER_PRINT_1.RX, U1.GPIO1
  GND: FINGER_PRINT_1.GND, U1.GND, LED.cathode, LED_2.cathode, LCM1602_IIC2.GND, Relay_1_Channel1.pin_2, POWER_SUPPLY_12V_5A.GND, BUZZER.pin1, S1.leg1
  N3: U1.GPIO33, S1.leg0
  N4: U1.GPIO26, Relay_1_Channel1.pin_3
  N5: U1.GPIO14, BUZZER.pin2
  N6: U1.GPIO11, Selenoid_Door_Lock.pin1
  N7: U1.GPIO2, R1.Pin_0
  N8: U1.GPIO0, R2.Pin_0
  N9: U1.GPIO21, LCM1602_IIC2.SDA
  N10: U1.GPIO22, LCM1602_IIC2.SCL
  N11: LED.anode, R1.Pin_1
  N12: LED_2.anode, R2.Pin_1
  VSS: LCM1602_IIC2.VSS, LCD_16x2_12C.VSS
  VDD: LCM1602_IIC2.VDD, LCD_16x2_12C.VDD
  N13: LCM1602_IIC2.V0, LCD_16x2_12C.V0
  N14: LCM1602_IIC2.RS, LCD_16x2_12C.RS
  N15: LCM1602_IIC2.RW, LCD_16x2_12C.R/W
  N16: LCM1602_IIC2.E, LCD_16x2_12C.E
  N17: LCM1602_IIC2.D0, LCD_16x2_12C.DB0
  N18: LCM1602_IIC2.D1, LCD_16x2_12C.DB1
  N19: LCM1602_IIC2.D2, LCD_16x2_12C.DB2
  N20: LCM1602_IIC2.D3, LCD_16x2_12C.DB3
  N21: LCM1602_IIC2.D4, LCD_16x2_12C.DB4
  N22: LCM1602_IIC2.D5, LCD_16x2_12C.DB5
  N23: LCM1602_IIC2.D6, LCD_16x2_12C.DB6
  N24: LCM1602_IIC2.D7, LCD_16x2_12C.DB7
  N25: LCM1602_IIC2.A, LCD_16x2_12C.LED+
  N26: LCM1602_IIC2.K, LCD_16x2_12C.LED-
  N27: Relay_1_Channel1.pin_4, Selenoid_Door_Lock.pin2
  N28: Relay_1_Channel1.pin_5, POWER_SUPPLY_12V_5A.+Vin

custom parts:
  Fingerprint Sensor: FINGERPRIN Sensor
  ESP32-38PinWide: Generic 38-Pin ESP32 with wide format (only access to one side of pins on a breadboard) based on Stephen Lilley's HiLetgo ESP-WROOM-32 ESP32 ESP-32S Development Board.
  LCM1602 IIC: I2C-Module to use a 1602 or 2004 LCD on with the wire.h libory Serial LCD Modul
  1 chan 5v relay module: 1 Channel 5V Relay Module Board Shield with Optocoupler Support High and Low Level Trigger for Arduino.
  PowerBRICK 12V: PowerBRICKs are split-rail power supply modules that are intended to be used with a breadboard. These generate both a negative and positive voltage out of a single 5V USB voltage.
  Buzzer: Fixed frequency buzzer
